# Fritzing sketch planche test (saved by Fritzing 0.9.3b)
breadboards: 1

parts:
  LED1 = RGB LED - (4 legs) [package="5 mm [THT]"]
  LED2 = RGB LED - (4 legs) [package="5 mm [THT]"]
  LED3 = RGB LED - (4 legs) [package="5 mm [THT]"]
  LED4 = RGB LED - (4 legs) [package="5 mm [THT]"]
  LED5 = RGB LED - (4 legs) [package="5 mm [THT]"]
  LED6 = RGB LED - (4 legs) [package="5 mm [THT]"]
  R1 = Resistor [tolerance=±5% resistance=220 package=THT]
  R2 = Resistor [tolerance=±5% resistance=220 package=THT]
  R3 = Resistor [tolerance=±5% resistance=220 package=THT]
  R4 = Resistor [tolerance=±5% resistance=220 package=THT]
  R5 = Resistor [tolerance=±5% resistance=220 package=THT]
  R6 = Resistor [tolerance=±5% resistance=220 package=THT]
  R7 = Resistor [tolerance=±5% resistance=220 package=THT]
  R8 = Resistor [tolerance=±5% resistance=220 package=THT]
  R9 = Resistor [tolerance=±5% resistance=220 package=THT]
  R10 = Resistor [tolerance=±5% resistance=220 package=THT]
  R11 = Resistor [tolerance=±5% resistance=220 package=THT]
  R12 = Resistor [tolerance=±5% resistance=220 package=THT]
  R13 = Resistor [tolerance=±5% resistance=220 package=THT]
  R14 = Resistor [tolerance=±5% resistance=220 package=THT]
  R15 = Resistor [tolerance=±5% resistance=220 package=THT]
  R16 = Resistor [tolerance=±5% resistance=220 package=THT]
  R17 = Resistor [tolerance=±5% resistance=220 package=THT]
  R18 = Resistor [tolerance=±5% resistance=220 package=THT]
  Composant1 = Arduino Uno (Rev3)
  LED7 = RGB LED - (4 legs) [package="5 mm [THT]"]
  R19 = Resistor [tolerance=±5% resistance=220 package=THT]
  R20 = Resistor [tolerance=±5% resistance=220 package=THT]
  R21 = Resistor [tolerance=±5% resistance=220 package=THT]

nets:
  N1: LED1.red_cathode, R6.Pin_0
  N2: LED1.common_anode, LED2.common_anode, LED3.common_anode, LED4.common_anode, LED5.common_anode, LED6.common_anode, Composant1.5V, LED7.common_anode
  N3: LED1.green_cathode, R7.Pin_0
  N4: LED1.blue_cathode, R1.Pin_0
  N5: LED2.red_cathode, R9.Pin_0
  N6: LED2.green_cathode, R8.Pin_0
  N7: LED2.blue_cathode, R2.Pin_0
  N8: LED3.red_cathode, R3.Pin_0
  N9: LED3.green_cathode, R4.Pin_0
  N10: LED3.blue_cathode, R5.Pin_0
  N11: LED4.red_cathode, R18.Pin_0
  N12: LED4.green_cathode, R17.Pin_0
  N13: LED4.blue_cathode, R16.Pin_0
  N14: LED5.red_cathode, R14.Pin_0
  N15: LED5.green_cathode, R13.Pin_0
  N16: LED5.blue_cathode, R15.Pin_0
  N17: LED6.red_cathode, R12.Pin_0
  N18: LED6.green_cathode, R11.Pin_0
  N19: LED6.blue_cathode, R10.Pin_0
  N20: R1.Pin_1, R5.Pin_1, Composant1.D0/RX
  N21: R2.Pin_1, R10.Pin_1, Composant1.D3_PWM
  N22: R3.Pin_1, R6.Pin_1, Composant1.D2
  N23: R4.Pin_1, R7.Pin_1, Composant1.D1/TX
  N24: R8.Pin_1, R11.Pin_1, Composant1.D4
  N25: R9.Pin_1, R12.Pin_1, Composant1.D5_PWM
  N26: R13.Pin_1, R17.Pin_1, Composant1.D7
  N27: R14.Pin_1, R18.Pin_1, Composant1.D8
  N28: R15.Pin_1, R16.Pin_1, Composant1.D6_PWM
  N29: Composant1.D9_PWM, R21.Pin_1
  N30: Composant1.D10_PWM/SS, R20.Pin_1
  N31: Composant1.D11_PWM/MOSI, R19.Pin_1
  N32: LED7.red_cathode, R21.Pin_0
  N33: LED7.green_cathode, R20.Pin_0
  N34: LED7.blue_cathode, R19.Pin_0
