# Fritzing sketch schema-capteur (saved by Fritzing 0.9.3b)

parts:
  WeMos_D1_Mini1 = WeMos D1 Mini
  Composant1 = Barometric Pressure Sensor - BMP085 Breakout
  U1 = GAS_SENSOR [package=mq-3]
  Composant2 = ws2812b [package="smd 2812b"]
  RHT1 = Humidity and Temperature Sensor RHT03

nets:
  N1: WeMos_D1_Mini1.3V3, U1.B1
  5V: WeMos_D1_Mini1.5V, Composant2.VDD
  N2: WeMos_D1_Mini1.A0, U1.H2
  N3: WeMos_D1_Mini1.D1, Composant1.SCL
  N4: WeMos_D1_Mini1.D2, Composant1.SDA
  N5: WeMos_D1_Mini1.D4, Composant2.DIN
  N6: WeMos_D1_Mini1.D6, RHT1.Data-signal
  N7: WeMos_D1_Mini1.G, Composant2.VSS
